# Fritzing sketch RipTide (saved by Fritzing 1.0.4)
stripboards: 1

parts:
  Part13 = InvenSense MPU6050
  Part14 = 24 NeoPixel Ring [part_number=1586]
  J10 = screw terminal, 2 pins
  Part9 = TFT 2.8 inch 320x240 Touch w microSD [part_number=1770]  # not connected
  J15 = Generic male header - 1 pins [form="♂ (male)" package=THT]  # not connected
  J17 = Generic male header - 1 pins [form="♂ (male)" package=THT]  # not connected
  J18 = Generic male header - 1 pins [form="♂ (male)" package=THT]  # not connected
  J21 = Generic male header - 1 pins [form="♂ (male)" package=THT]  # not connected
  J23 = Generic male header - 1 pins [form="♂ (male)" package=THT]  # not connected
  F2 = Resettable Fuse PTC [package=ptc]  # not connected
  C2 = Electrolytic Capacitor [capacitance=4.7mF voltage=16V package="100 mil [THT, electrolytic]"]
  J24 = Generic male header - 1 pins [form="♂ (male)" package=THT]  # not connected
  J25 = Generic male header - 1 pins [form="♂ (male)" package=THT]  # not connected
  Part20 = Adafruit Breadboard-Friendly NeoPixel [part_number="Adafruit #1312"]
  S6 = Reed switch [package=THT]
  J27 = Generic male header - 1 pins [form="♂ (male)" package=THT]  # not connected
  J3 = rounded female pin header, 12 pins [form="♀ (female rounded)"]  # not connected
  J29 = Generic male header - 1 pins [form="♂ (male)" package=THT]  # not connected
  J31 = Generic male header - 1 pins [form="♂ (male)" package=THT]  # not connected
  J32 = Generic male header - 1 pins [form="♂ (male)" package=THT]  # not connected
  J33 = Generic male header - 1 pins [form="♂ (male)" package=THT]  # not connected
  J35 = Generic male header - 1 pins [form="♂ (male)" package=THT]  # not connected
  J36 = rounded female pin header, 4 pins [form="♀ (female rounded)"]  # not connected
  J37 = Generic male header - 1 pins [form="♂ (male)" package=THT]  # not connected
  J40 = Generic male header - 1 pins [form="♂ (male)" package=THT]  # not connected
  M1 = xy-mos d4184 [package=THT]
  J41 = Generic male header - 1 pins [form="♂ (male)" package=THT]
  J42 = Generic male header - 1 pins [form="♂ (male)" package=THT]
  J43 = Generic male header - 1 pins [form="♂ (male)" package=THT]  # not connected
  M2 = xy-mos d4184 [package=THT]
  J46 = Generic male header - 1 pins [form="♂ (male)" package=THT]  # not connected
  J26 = rounded female pin header, 4 pins [form="♀ (female rounded)"]  # not connected
  J48 = screw terminal, 2 pins  # not connected
  J50 = screw terminal, 2 pins  # not connected
  J51 = Generic male header - 1 pins [form="♂ (male)" package=THT]  # not connected
  J53 = Generic male header - 1 pins [form="♂ (male)" package=THT]  # not connected
  J52 = rounded female pin header, 3 pins [form="♀ (female rounded)"]  # not connected
  J54 = screw terminal, 2 pins
  J8 = rounded female pin header, 12 pins [form="♀ (female rounded)"]  # not connected
  J44 = rounded female pin header, 12 pins [form="♀ (female rounded)"]  # not connected
  J47 = single row smd female pin header, 1 pin [form="♀ (female)"]  # not connected
  J55 = Generic male header - 1 pins [form="♂ (male)" package=THT]  # not connected
  F3 = Resettable Fuse PTC [package=ptc]  # not connected
  F4 = Resettable Fuse PTC [package=ptc]  # not connected
  J56 = Generic male header - 1 pins [form="♂ (male)" package=THT]  # not connected
  J57 = Generic male header - 1 pins [form="♂ (male)" package=THT]  # not connected
  J59 = Generic male header - 1 pins [form="♂ (male)" package=THT]  # not connected
  R13 = Resistor [tolerance=±5% power=0.25W resistance=4.7k package=THT]  # not connected
  C7 = Electrolytic Capacitor [capacitance=4.7mF voltage=16V package="100 mil [THT, electrolytic]"]
  R7 = Resistor [tolerance=±5% power=0.25W resistance=47k package=THT]
  R8 = Resistor [tolerance=±5% power=0.25W resistance=47k package=THT]
  R9 = Resistor [tolerance=±5% power=0.25W resistance=47k package=THT]
  J60 = Generic male header - 1 pins [form="♂ (male)" package=THT]
  J61 = Generic male header - 1 pins [form="♂ (male)" package=THT]
  J62 = Generic male header - 1 pins [form="♂ (male)" package=THT]
  J63 = Generic male header - 1 pins [form="♂ (male)" package=THT]
  J64 = Generic male header - 1 pins [form="♂ (male)" package=THT]
  U1 = TRANSISTOR_NPN [package=to-92]
  J66 = Generic male header - 1 pins [form="♂ (male)" package=THT]
  R11 = Resistor [tolerance=±5% power=0.25W resistance=1k package=THT]
  D1 = Diode [package=diode-hv]
  R12 = Resistor [tolerance=±5% power=0.25W resistance=470 package=THT]
  Part21 = 24 NeoPixel Ring [part_number=1586]
  1µF = Capacitor [package=cap-pth-small2]  # not connected
  0_1µF = Capacitor [package=cap-pth-small2]  # not connected
  S7 = Reed switch [package=THT]
  R14 = Resistor [tolerance=±5% power=0.25W resistance=47k package=THT]
  J67 = Generic male header - 1 pins [form="♂ (male)" package=THT]
  S8 = Reed switch [package=THT]  # not connected
  J65 = Piezo Speaker  # not connected
  0_1µF_2 = Capacitor [package=cap-pth-small2]
  0_1µF_3 = Capacitor [package=cap-pth-small2]
  0_1µF_4 = Capacitor [package=cap-pth-small2]  # not connected
  DS6 = DS18B20 1-Wire Temperature Sensor [part_number=DS18B20]  # not connected
  0_1µF_5 = Capacitor [package=cap-pth-small2]  # not connected
  DS7 = DS18B20 1-Wire Temperature Sensor [part_number=DS18B20]  # not connected
  0_1µF_6 = Capacitor [package=cap-pth-small2]  # not connected
  0_1µF_7 = Capacitor [package=cap-pth-small2]  # not connected
  DS8 = DS18B20 1-Wire Temperature Sensor [part_number=DS18B20]  # not connected
  DS9 = DS18B20 1-Wire Temperature Sensor [part_number=DS18B20]  # not connected
  0_1µF_8 = Capacitor [package=cap-pth-small2]  # not connected
  DS10 = DS18B20 1-Wire Temperature Sensor [part_number=DS18B20]  # not connected
  0_1µF_9 = Capacitor [package=cap-pth-small2]
  Part22 = Adafruit Breadboard-Friendly NeoPixel [part_number="Adafruit #1312"]
  R15 = Resistor [tolerance=±5% power=0.25W resistance=470 package=THT]  # not connected
  S9 = Reed switch [package=THT]  # not connected
  S10 = Reed switch [package=THT]  # not connected
  Q1 = Basic FET N-Channel [package="TO220 [THT]"]
  D2 = Zener Diode [part_number=1N4732A breakdown_voltage=12.1V package="300 mil [THT]"]  # not connected
  R18 = Resistor [tolerance=±5% power=0.25W resistance=10k package=THT]
  R19 = Resistor [tolerance=±5% power=0.25W resistance=6.8k package=THT]  # not connected

nets:
  N1: Part13.VCC, 0_1µF_9.2
  N2: Part14.IN, R12.Pin_1
  N3: Part14.OUT, Part21.IN
  VDD: Part14.VDD, Part21.VDD, 0_1µF_2.1, 0_1µF_3.1
  GND: Part14.GND, Part21.GND, 0_1µF_2.2, 0_1µF_3.2
  N4: J10.pin2, Q1.drain
  N5: C2.-, J64.Ground
  GND_2: Part20.GND, Part22.GND
  VDD_2: Part20.VDD, Part22.VDD
  N6: Part20.OUT, Part22.IN
  N7: S6.pin_1, S7.pin_1
  N8: S6.pin_2, J54.pin1, S7.pin_2
  N9: M1.pin1, M1.pin3, M1.pin4
  N10: M1.pin2, M1.pin5, M1.pin6, M1.pin7, J42.Ground
  N11: J41.Ground, M2.pin2, M2.pin5, M2.pin6, M2.pin7
  N12: M2.pin1, M2.pin3, M2.pin4
  N13: C7.-, J63.Ground
  N14: R7.Pin_0, J62.Ground
  N15: R8.Pin_0, J60.Ground
  N16: R9.Pin_0, J61.Ground
  N17: U1.E, D1.A
  N18: U1.B, R11.Pin_1
  N19: U1.C, J66.Ground
  N20: R14.Pin_0, J67.Ground
  N21: Q1.gate, R18.Pin_0

notes:
  Display
  Reset
  SPI Clock
  I2C SCL
  Data cmd
  MISO
  MOSI
  Chip select
  Led backlight
  SD Card
  Throttle/btns
  Gyro
  Pressure
  Throttleds
  5v
  3.3v
  Pixels
  ESC
  One wire
  Extra
  Buzzer
  BMS
  N/C
  Fuse
  47K Pull down
  4.7K Pull up
  I2C SDA
  12.1V Zener
  Mains kill switch

custom parts:
  24 NeoPixel Ring: 24 ultra bright smart LED NeoPixels are arranged in a circle with 2.6" (66mm) outer diameter. The rings are 'chainable' - connect the output pin of one to the input pin of another. Use only one microcontroller pin to control as many as you can chain together! Each LED is addressable as the driver chip is inside the LED. Each one has ~18mA constant current drive so the color will be very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
  TFT 2.8 inch 320x240 Touch w microSD: This TFT display is big (2.8" diagonal) bright (4 white-LED backlight) and colorful! 240x320 pixels with individual RGB pixel control. As a bonus, this display has a resistive touchscreen attached to it already, so you can detect finger presses anywhere on the screen.
  Generic male header - 1 pins: Generic male header
  Adafruit Breadboard-Friendly NeoPixel: This is the easiest way possible to add small, bright RGB pixels to your project. We took the same technology from our Flora NeoPixels and made them breadboard friendly, with two rows of 3 x 0.1" spaced header on each side for easy soldering, chaining and breadboarding. These ultra-bright LEDs have a constant-current driver cooked right into the LED package! The pixels are chainable - so you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
  xy-mos d4184: xy-mos d4184 Two parallel N-Channel logic compatible MOSFETS with low Rds(on) for high current low-side switching applications.
